// Logisim project GangeMedTi.circ as structural Verilog
module Half_Adder (
  input  X_inn,
  input  Y_inn,
  output Sum,
  output Cout
);

  and and_1 (Cout, X_inn, Y_inn);
  xor xor_1 (Sum, X_inn, Y_inn);
endmodule

module Full_Adder (
  input  X_inn,
  input  Y_inn,
  input  C_inn,
  output Sum,
  output Cout
);

  wire and_1_out, and_2_out, and_3_out, xor_1_out;

  xor xor_1 (xor_1_out, X_inn, Y_inn);
  and and_1 (and_1_out, X_inn, Y_inn);
  and and_2 (and_2_out, X_inn, C_inn);
  and and_3 (and_3_out, C_inn, Y_inn);
  xor xor_2 (Sum, xor_1_out, C_inn);
  or or_1 (Cout, and_1_out, and_2_out, and_3_out);
endmodule
